# Fritzing sketch smart_fan_arduino (saved by Fritzing 0.9.5d)
breadboards: 1

parts:
  R1 = Resistor [tolerance=±5% resistance=1k package=THT]
  R2 = Resistor [tolerance=±5% resistance=220 package=THT]
  R3 = Resistor [tolerance=±5% resistance=220 package=THT]
  R4 = Resistor [tolerance=±5% resistance=10k package=THT]
  R5 = Resistor [tolerance=±5% resistance=4.7k package=THT]
  D1 = Rectifier Diode [part_number=1N4007 package="300 mil [THT]"]
  OLED_I2C1 = OLED 128x64 I2C Monochrome Display
  LED1 = LED - 5mm [color="Green (565nm)" package="5 mm [THT]"]
  NPN_2N2222A = NPN-Transistor [package="TO92 [THT]"]
  DS1 = DS18B20 1-Wire Temperature Sensor [part_number=DS18B20]
  Cooling_Fan_12W/0_15A = DC Motor
  Компонент2 = Arduino Nano (Rev3.0)
  12V/3A_power_supply = Power plug
  LED2 = LED - 5mm [color="Red (633nm)" package="5 mm [THT]"]

nets (from the schematic view):
  N1: R1.Pin_0, NPN_2N2222A.B
  N2: R1.Pin_1, Компонент2.D3
  N3: R2.Pin_0, Компонент2.D7
  N4: R2.Pin_1, LED2.anode
  N5: R3.Pin_0, Компонент2.D8
  N6: R3.Pin_1, LED1.anode
  N7: R4.Pin_0, NPN_2N2222A.E
  N8: R4.Pin_1, D1.anode, NPN_2N2222A.C, Cooling_Fan_12W/0_15A.pin_2
  VDD: R5.Pin_0, OLED_I2C1.VDD, DS1.VDD, Компонент2.5V
  N9: R5.Pin_1, DS1.DQ, Компонент2.D2
  12V: D1.cathode, Cooling_Fan_12W/0_15A.pin_1, Компонент2.VIN, 12V/3A_power_supply.VCC
  N10: OLED_I2C1.SDA, Компонент2.A4
  N11: OLED_I2C1.SCK, Компонент2.A5
  GND: OLED_I2C1.GND, LED1.cathode, DS1.GND, Компонент2.GND, 12V/3A_power_supply.GND, LED2.cathode
